# Fritzing sketch exemplo ligacoes (saved by Fritzing 0.9.3b)
breadboards: 1

parts:
  JP22 = Header 2 [package=screwterminal-3.5mm-2_lock]
  JP23 = Header 2 [package=screwterminal-3.5mm-2_lock]
  JP24 = Header 3 [package=screwterminal-3.5mm-3_lock.007s]
  JP25 = Header 3 [package=screwterminal-3.5mm-3_lock.007s]
  Q2 = PHOTOTRANSISTOR REFLECTIVE OBJECT SENSOR [package=qrb1114-side]
  LED9 = LED - 5mm [color="Red (633nm)" package="5 mm [THT]"]
  LED10 = LED - 5mm [color="Red (633nm)" package="5 mm [THT]"]
  LED11 = LED - 5mm [color="Red (633nm)" package="5 mm [THT]"]
  LED12 = LED - 5mm [color="Red (633nm)" package="5 mm [THT]"]
  LED13 = LED - 5mm [color="Red (633nm)" package="5 mm [THT]"]
  LED14 = LED - 5mm [color="Red (633nm)" package="5 mm [THT]"]
  LED15 = LED - 5mm [color="Red (633nm)" package="5 mm [THT]"]
  LED16 = LED - 5mm [color="Red (633nm)" package="5 mm [THT]"]
  S4 = SPST Switch [package=r_sw_th]
  S5 = SPST Switch [package=r_sw_th]
  S6 = SWITCH-MOMENTARY-2 [package=tactile_switch_tall]

nets:
  N1: JP22.1, S6.1
  N2: JP22.2, S6.2
  N3: JP23.1, LED9.anode, LED10.anode, LED11.anode, LED12.anode, LED13.anode, LED14.anode, LED15.anode, LED16.anode
  N4: JP23.2, LED9.cathode, LED10.cathode, LED11.cathode, LED12.cathode, LED13.cathode, LED14.cathode, LED15.cathode, LED16.cathode
  N5: JP24.1, S4.S
  N6: JP24.2, S5.S
  N7: JP24.3, S4.P, S5.P
  N8: JP25.1, Q2.E, Q2.K
  N9: JP25.2, Q2.A
  N10: JP25.3, Q2.C

notes:
  COMUM
  P1
  emissor+
  FC1
  emissor-
  FC2
  exemplo de como ligar os sensores
  5V
  L1
  GND
  START
  EXEMPLO DE COM0 LIGAR OS LEDS
  BOTÃO START
  EXEMPLO DE COM0 LIGAR OS FIMS DE CURSO
