# Fritzing sketch display1 (saved by Fritzing 0.9.3b)
breadboards: 1

parts:
  DI3 = 7-Segment LED Display [package=THT]
  R1 = Resistor [tolerance=±5% resistance=4.7k package=THT]
  R2 = Resistor [tolerance=±5% resistance=4.7k package=THT]
  JP9 = Header 4 [package=screwterminal-3.5mm-4_lock]
  JP10 = Header 4 [package=screwterminal-3.5mm-4_lock]
  Q1 = pnp-Powertransistor [part_number=TIP127 package="TO220 [THT]"]
  Q2 = pnp-Powertransistor [part_number=TIP127 package="TO220 [THT]"]
  DI4 = 7-Segment LED Display [package=THT]
  R3 = Resistor [tolerance=±5% resistance=1k package=THT]
  R4 = Resistor [tolerance=±5% resistance=1k package=THT]
  R5 = Resistor [tolerance=±5% resistance=1k package=THT]
  R6 = Resistor [tolerance=±5% resistance=1k package=THT]
  R7 = Resistor [tolerance=±5% resistance=1k package=THT]
  C3 = Ceramic Capacitor [capacitance=100nF package="100 mil [THT, multilayer]"]
  U2 = 74HC595 [package="DIP16 [THT]"]
  JP8 = Header 4 [package=screwterminal-3.5mm-4_lock]
  JP11 = Header 4 [package=screwterminal-3.5mm-4_lock]
  IC1 = ULN2003A [package="DIP16 [THT]"]
  R8 = Resistor [tolerance=±5% resistance=1k package=THT]
  R9 = Resistor [tolerance=±2% resistance=1k package=THT]

nets:
  N1: DI3.cathodeE, JP10.1, DI4.cathodeE, R8.Pin_0
  N2: DI3.cathodeD, JP10.2, DI4.cathodeD, R7.Pin_0
  N3: DI3.commAnode, Q2.collector
  N4: DI3.cathodeC, JP10.3, DI4.cathodeC, R6.Pin_0
  N5: DI3.cathodeB, JP9.1, DI4.cathodeB, R9.Pin_0
  N6: DI3.cathodeA, JP9.2, DI4.cathodeA, R4.Pin_0
  N7: DI3.cathodeF, JP9.3, DI4.cathodeF, R5.Pin_0
  N8: DI3.cathodeG, JP9.4, DI4.cathodeG, R3.Pin_0
  N9: R1.Pin_0, JP11.4
  N10: R1.Pin_1, Q1.base
  N11: R2.Pin_0, JP11.3
  N12: R2.Pin_1, Q2.base
  N13: Q1.collector, DI4.commAnode
  N14: Q1.emitter, JP11.2, IC1.COM_-_Common
  N15: R3.Pin_1, IC1.Out_4
  N16: R4.Pin_1, IC1.Out_2
  N17: R5.Pin_1, IC1.Out_3
  N18: R6.Pin_1, IC1.Out_7
  N19: R7.Pin_1, IC1.Out_6
  GND: C3.0, U2.GND, U2.OE, JP11.1, IC1.0V
  N20: C3.1, U2.MR, U2.VCC, JP8.4
  B: U2.Q1, IC1.In_3
  C: U2.Q2, IC1.In_2
  D: U2.Q3, IC1.In_1
  E: U2.Q4, IC1.In_5
  F: U2.Q5, IC1.In_6
  G: U2.Q6, IC1.In_7
  N21: U2.SH_CP, JP8.3
  N22: U2.ST_CP, JP8.2
  N23: U2.DS, JP8.1
  A: U2.Q0, IC1.In_4
  N24: IC1.Out_5, R8.Pin_1
  N25: IC1.Out_1, R9.Pin_1

notes:
  1
  2
  12V
  6
  5
  7
  5V
  GND
  todos esses resistores são de 1K
  8
  9
  10
  11
  12
  14
  13
  (A)
  (B)
  (C)
  (D)
  (E)
  (F)
  (G)
  SEGMENTO DO DISPLAY
