# Fritzing sketch display2 (saved by Fritzing 0.9.3b)
breadboards: 1

parts:
  DI4 = 7-Segment LED Display [package=THT]
  part = Resistor [tolerance=±5% resistance=4.7k package=THT]
  part_2 = Header 4 [package=screwterminal-3.5mm-4_lock]
  part_3 = Resistor [tolerance=±5% resistance=4.7k package=THT]
  part_4 = pnp-Powertransistor [part_number=TIP127 package="TO220 [THT]"]
  part_5 = Header 4 [package=screwterminal-3.5mm-4_lock]
  DI3 = 7-Segment LED Display [package=THT]
  part_6 = pnp-Powertransistor [part_number=TIP127 package="TO220 [THT]"]
  JP6 = Header 4 [package=screwterminal-3.5mm-4_lock]

nets:
  N1: DI4.cathodeE, part_2.1, DI3.cathodeE
  N2: DI4.cathodeD, part_2.2, DI3.cathodeD
  N3: DI4.commAnode, part_4.collector
  N4: DI4.cathodeC, part_2.3, DI3.cathodeC
  N5: DI4.cathodeB, part_5.1, DI3.cathodeB
  N6: DI4.cathodeA, part_5.2, DI3.cathodeA
  N7: DI4.cathodeF, part_5.3, DI3.cathodeF
  N8: DI4.cathodeG, part_5.4, DI3.cathodeG
  N9: part.Pin_0, JP6.1
  N10: part.Pin_1, part_4.base
  N11: part_3.Pin_0, JP6.2
  N12: part_3.Pin_1, part_6.base
  N13: part_4.emitter, part_6.emitter, JP6.3
  N14: DI3.commAnode, part_6.collector

notes:
  12
  14
  13
  (A)
  (C)
  (F)
  (E)
  (G)
  (B)
  (D)
  SEGMENTO DO DISPLAY
  3
  4
  12V
  8
  10
  9
  11
