# Fritzing sketch placaPrincipal-parte2 (saved by Fritzing 0.9.3b)
breadboards: 1

parts:
  R14 = Resistor [tolerance=±5% resistance=10k package=THT]
  R15 = Resistor [tolerance=±5% resistance=10k package=THT]
  R16 = Resistor [tolerance=±5% resistance=10k package=THT]
  R17 = Resistor [tolerance=±5% resistance=10k package=THT]
  R18 = Resistor [tolerance=±5% resistance=10k package=THT]
  R19 = Resistor [tolerance=±5% resistance=10k package=THT]
  R20 = Resistor [tolerance=±5% resistance=10k package=THT]
  R21 = Resistor [tolerance=±5% resistance=10k package=THT]
  R22 = Resistor [tolerance=±5% resistance=10k package=THT]
  R23 = Resistor [tolerance=±5% resistance=10k package=THT]
  JP11 = Header 2 [package=screwterminal-3.5mm-2_lock]
  JP12 = Header 2 [package=screwterminal-3.5mm-2_lock]
  R24 = Resistor [tolerance=±5% resistance=220 package=THT]
  SG2 = Buzzer 12mm [package=buzzer-ccv-kit]
  C7 = Ceramic Capacitor [capacitance=100nF package="100 mil [THT, multilayer]"]
  C8 = Ceramic Capacitor [capacitance=100nF package="100 mil [THT, multilayer]"]
  U5 = 74HC4051 [package=so16]
  U6 = 74HC595 [package="DIP16 [THT]"]
  JP13 = Header 4 [package=jst-4-pth]
  JP14 = Header 4 [package=jst-4-pth]
  JP15 = Header 3 [package=screwterminal-3.5mm-3_lock.007s]
  U7 = Voltage Regulator - 5V [package="DPak [SMD]"]
  C9 = Electrolytic Capacitor [part_number=0.33uF capacitance=1µF package="100 mil [THT, electrolytic]"]
  C10 = Electrolytic Capacitor [part_number=0.33uF capacitance=1µF package="100 mil [THT, electrolytic]"]
  Q2 = NPN-Transistor [part_number=TIP122 package="TO92 [THT]"]
  R25 = Resistor [tolerance=±5% resistance=4.7k package=THT]

nets:
  FC2: R14.Pin_0, JP15.2
  5V: R14.Pin_1, R15.Pin_1, R16.Pin_0, R17.Pin_0, R18.Pin_0, R19.Pin_0, R20.Pin_1, R21.Pin_1, R22.Pin_1, R23.Pin_1, R24.Pin_1, C7.1, C8.1, U5.VDD, U6.MR, U6.VCC, U7.output_voltage, C10.+
  FC1: R15.Pin_0, JP15.3
  P6: R16.Pin_1, U5.IO5, JP13.2
  P4: R17.Pin_1, U5.IO3, JP13.4
  P5: R18.Pin_1, U5.IO4, JP13.3
  P7: R19.Pin_1, U5.IO6, JP13.1
  P3: R20.Pin_0, U5.IO2, JP14.1
  P2: R21.Pin_0, U5.IO1, JP14.2
  P1: R22.Pin_0, U5.IO0, JP14.3
  START: R23.Pin_0, U5.IO7, JP14.4
  GND: JP11.1, JP12.1, SG2.1, C7.0, C8.0, U5.INH, U5.VEE, U5.VSS, U6.GND, U6.OE, JP15.1, U7.GND, C9.-, C10.-
  N1: JP11.2, U7.input_voltage, C9.+
  N2: SG2.2, Q2.E
  Entrada: U5.IO
  CC: U5.C
  CB: U5.B
  CA: U5.A
  L2: U6.Q1
  L3: U6.Q2
  L4: U6.Q3
  L5: U6.Q4
  L6: U6.Q5
  L7: U6.Q6
  N3: U6.Q7, R25.Pin_1
  CLK2: U6.SH_CP
  LATCH2: U6.ST_CP
  DATA2: U6.DS
  L1: U6.Q0
  N4: Q2.B, R25.Pin_0
  12V: Q2.C

notes:
  Alimentação dos sensores
  buzzer
  fim de curso
  Conector dos sensores
  FC1
  COMUM
  FC2
  12V
  GND
  REGULADOR 7805
  0.33uF
  0.1uF
  resistores de 10K
  P1
  P5
  P2
  P6
  P4
  P7
  P3
  sensores dos pinos - receptor
  botão start
  emissor+
  emissor-
