# Fritzing sketch placaPrincipal (saved by Fritzing 0.9.3b)
breadboards: 1

parts:
  R6 = Resistor [tolerance=±5% resistance=10k package=THT]
  R8 = Resistor [tolerance=±5% resistance=10k package=THT]
  U4 = Voltage Regulator - 5V [package="DPak [SMD]"]
  Q2 = NPN-Transistor [part_number=TIP122 package="TO92 [THT]"]
  JP17 = Header 2 [package=screwterminal-3.5mm-2_lock]
  JP7 = Header 4 [package=jst-4-pth]
  R7 = Resistor [tolerance=±5% resistance=10k package=THT]
  JP18 = Header 3 [package=screwterminal-3.5mm-3_lock.007s]
  C1 = Ceramic Capacitor [capacitance=100nF package="100 mil [THT, multilayer]"]
  R5 = Resistor [tolerance=±5% resistance=10k package=THT]
  SG1 = Buzzer 12mm [package=buzzer-ccv-kit]
  R4 = Resistor [tolerance=±5% resistance=10k package=THT]
  JP19 = Header 2 [package=screwterminal-3.5mm-2_lock]
  R3 = Resistor [tolerance=±5% resistance=10k package=THT]
  U2 = 74HC595 [package="DIP16 [THT]"]
  U3 = 74HC4051 [package=so16]
  JP6 = Header 4 [package=jst-4-pth]
  C5 = Electrolytic Capacitor [capacitance=1µF part_number=0.33uF package="100 mil [THT, electrolytic]"]
  R19 = Resistor [tolerance=±5% resistance=10k package=THT]
  C6 = Electrolytic Capacitor [capacitance=1µF part_number=0.33uF package="100 mil [THT, electrolytic]"]
  R2 = Resistor [tolerance=±5% resistance=10k package=THT]
  R23 = Resistor [tolerance=±5% resistance=10k package=THT]
  R21 = Resistor [tolerance=±5% resistance=10k package=THT]
  R22 = Resistor [tolerance=±5% resistance=4.7k package=THT]
  R20 = Resistor [tolerance=±5% resistance=220 package=THT]
  C3 = Ceramic Capacitor [capacitance=100nF package="100 mil [THT, multilayer]"]
  Q3 = NPN-Transistor [part_number=TIP122 package="TO92 [THT]"]
  part = Resistor [tolerance=±5% resistance=4.7k package=THT]
  JP32 = Header 3 [package=screwterminal-3.5mm-3_lock.007s]
  JP33 = Header 3 [package=screwterminal-3.5mm-3_lock.007s]
  JP34 = Header 3 [package=screwterminal-3.5mm-3_lock.007s]
  Q4 = NPN-Transistor [part_number=TIP122 package="TO92 [THT]"]
  IC5 = ULN2003A [package="DIP16 [THT]"]
  R28 = Resistor [tolerance=±5% resistance=220 package=THT]
  R29 = Resistor [tolerance=±5% resistance=220 package=THT]
  R30 = Resistor [tolerance=±5% resistance=220 package=THT]
  R31 = Resistor [tolerance=±5% resistance=220 package=THT]
  R32 = Resistor [tolerance=±5% resistance=220 package=THT]
  R33 = Resistor [tolerance=±5% resistance=220 package=THT]
  R34 = Resistor [tolerance=±5% resistance=220 package=THT]
  R35 = Resistor [tolerance=±5% resistance=4.7k package=THT]
  R36 = Resistor [tolerance=±5% resistance=10k package=THT]
  JP35 = Header 2 [package=screwterminal-3.5mm-2_lock]
  JP36 = Header 2 [package=screwterminal-3.5mm-2_lock]
  IC6 = H-Bridge [package=THT]
  Componente3 = Arduino Nano (Rev3.0)
  JP37 = Header 4 [package=jst-4-pth]
  JP38 = Header 4 [package=jst-4-pth]
  D12 = Rectifier Diode [part_number=1N4001 package="300 mil [THT]"]
  D13 = Rectifier Diode [part_number=1N4001 package="300 mil [THT]"]
  D14 = Rectifier Diode [part_number=1N4001 package="300 mil [THT]"]
  D15 = Rectifier Diode [part_number=1N4001 package="300 mil [THT]"]

nets:
  5V: R6.Pin_0, R8.Pin_0, U4.output_voltage, Q2.C, R7.Pin_0, C1.1, R5.Pin_0, R4.Pin_1, R3.Pin_1, U2.MR, U2.VCC, U3.VDD, C5.+, R19.Pin_1, R2.Pin_1, R23.Pin_1, R21.Pin_1, C3.1, Q3.C, JP34.1, IC5.COM_-_Common, R36.Pin_1, IC6.VCC2, IC6.VCC1, Componente3.VIN, D12.cathode, D13.cathode
  P5: R6.Pin_1, U3.IO4, JP6.3
  P6: R8.Pin_1, U3.IO5, JP6.2
  N1: U4.input_voltage, JP17.2, C6.+
  GND: U4.GND, JP17.1, JP18.1, C1.0, SG1.1, JP19.1, U2.GND, U2.OE, U3.INH, U3.VEE, U3.VSS, C5.-, C6.-, C3.0, JP34.3, Q4.E, IC5.0V, IC6.GND1, IC6.GND2, IC6.GND3, IC6.GND4, Componente3.GND, D14.anode, D15.anode
  N2: Q2.E, SG1.2
  N3: Q2.B, R22.Pin_0
  P3: JP7.1, R4.Pin_0, U3.IO2
  P2: JP7.2, R3.Pin_0, U3.IO1
  P1: JP7.3, U3.IO0, R2.Pin_0
  START: JP7.4, U3.IO7, R23.Pin_0
  P4: R7.Pin_1, U3.IO3, JP6.4
  FC2: JP18.2, R21.Pin_0, Componente3.A2
  FC1: JP18.3, R19.Pin_0, Componente3.A3
  P7: R5.Pin_1, U3.IO6, JP6.1
  N4: JP19.2, R20.Pin_0
  L2: U2.Q1, R33.Pin_0
  L3: U2.Q2, R32.Pin_0
  L4: U2.Q3, R31.Pin_0
  L5: U2.Q4, R30.Pin_0
  L6: U2.Q5, R29.Pin_0
  L7: U2.Q6, R28.Pin_0
  N5: U2.Q7, R22.Pin_1
  CLK: U2.SH_CP, JP32.2, JP33.2, Componente3.D8
  LATCH: U2.ST_CP, Componente3.D7
  DATA: U2.DS, JP32.1, JP33.1, Componente3.D9
  L1: U2.Q0, R34.Pin_0
  Entrada: U3.IO, Componente3.A4
  CC: U3.C, Componente3.A7
  CB: U3.B, Componente3.A6
  CA: U3.A, Componente3.A5
  N6: R20.Pin_1, Q3.E
  N7: Q3.B, part.Pin_0
  EMISSOR: part.Pin_1, Componente3.A1
  N8: JP32.3, Componente3.D10
  N9: JP33.3, Componente3.D11/MOSI
  12V: JP34.2, JP35.1
  N10: Q4.B, R35.Pin_0
  N11: Q4.C, JP35.2
  N12: IC5.In_1, R34.Pin_1
  N13: IC5.In_2, R33.Pin_1
  N14: IC5.In_3, R32.Pin_1
  N15: IC5.In_4, R31.Pin_1
  N16: IC5.In_5, R30.Pin_1
  N17: IC5.In_6, R29.Pin_1
  N18: IC5.In_7, R28.Pin_1
  N19: IC5.Out_7, JP38.3
  N20: IC5.Out_6, JP38.2
  N21: IC5.Out_5, JP38.1
  N22: IC5.Out_4, JP37.4
  N23: IC5.Out_3, JP37.3
  N24: IC5.Out_2, JP37.2
  N25: IC5.Out_1, JP37.1
  N26: R35.Pin_1, Componente3.A0
  N27: R36.Pin_0, IC6.1_2EN
  N28: JP36.1, IC6.1Y, D12.anode, D15.cathode
  N29: JP36.2, IC6.2Y, D13.anode, D14.cathode
  M1: IC6.1A, Componente3.D3
  M2: IC6.2A, Componente3.D2

notes:
  D
  E
  COMUM
  FC2
  P2
  Conector dos sensores
  P6
  0.1uF
  P1
  emissor-
  P4
  P3
  P7
  buzzer
  emissor+
  resistores de 10K
  sensores dos pinos - receptor
  GND
  0.33uF
  botão start
  Alimentação dos sensores
  FC1
  fim de curso
  REGULADOR 7805
  P5
  12V
  5V
  B
  A
  C
  L7
  L6
  L5
  L4
  L3
  L2
  L1
  resistores de 220R
  LIGAR 5V OU 12V
  SAÍDA ALERTA VITÓRIA
  conector dos displays
  Conectar a todos os displays
  RECORDE
  TEMPO
  saída motor
  Conectores dos leds
