# Fritzing sketch placaPrincipal (saved by Fritzing 0.9.3b)
breadboards: 1

parts:
  Componente1 = Arduino Nano (Rev3.0) (ICSP)
  U6 = 74HC4051 [package=so16]
  R46 = Resistor [tolerance=±5% resistance=3.3k package=THT]
  R47 = Resistor [tolerance=±5% resistance=220 package=THT]
  R48 = Resistor [tolerance=±5% resistance=220 package=THT]
  R49 = Resistor [tolerance=±5% resistance=220 package=THT]
  R50 = Resistor [tolerance=±5% resistance=220 package=THT]
  R51 = Resistor [tolerance=±5% resistance=3.3k package=THT]
  R52 = Resistor [tolerance=±5% resistance=220 package=THT]
  R53 = Resistor [tolerance=±5% resistance=220 package=THT]
  R54 = Resistor [tolerance=±5% resistance=220 package=THT]
  R55 = Resistor [tolerance=±5% resistance=220 package=THT]
  JP30 = Header 10 [package=1x10-2mm-smd]
  JP35 = Header 3 [package=screwterminal-3.5mm-3_lock.007s]
  JP36 = Header 5 [package=1x05-1mm]
  JP37 = Header 2 [package=springterminal-2.54mm-2]
  D1 = Rectifier Diode [part_number=1N4001 package="Melf DO-213 AB [SMD]"]
  JP38 = Header 2 [package=springterminal-2.54mm-2]
  Q24 = NPN-Transistor [part_number=TIP122 package="TO92 [THT]"]
  R56 = Resistor [tolerance=±5% resistance=2.2k package=THT]
  Q25 = NPN-Transistor [part_number=TIP122 package="TO92 [THT]"]
  R57 = Resistor [tolerance=±2% resistance=1.5k package=THT]
  Q26 = NPN-Transistor [part_number=BC548 package="TO92 [THT]"]
  R58 = Resistor [tolerance=±5% resistance=1.5k package=THT]
  JP39 = Header 2 [package=springterminal-2.54mm-2]
  R59 = Resistor [tolerance=±5% resistance=470 package=THT]
  JP40 = Header 2 [package=springterminal-2.54mm-2]
  R60 = Resistor [tolerance=±5% resistance=10k package=THT]
  C12 = Ceramic Capacitor [capacitance=100nF package="100 mil [THT, multilayer]"]
  JP41 = Header 1 [package=pad-1.5x4.5]
  Q121 = NPN-Transistor [package="TO92 [THT]"]
  R245 = Resistor [tolerance=±5% resistance=220 package=THT]
  Q122 = NPN-Transistor [package="TO92 [THT]"]
  R254 = Resistor [tolerance=±5% resistance=220 package=THT]
  R250 = Resistor [tolerance=±5% resistance=220 package=THT]
  R227 = Resistor [tolerance=±5% resistance=220 package=THT]
  Q112 = NPN-Transistor [package="TO92 [THT]"]
  C34 = Electrolytic Capacitor [capacitance=1µF part_number=0.33uF package="100 mil [THT, electrolytic]"]
  C33 = Electrolytic Capacitor [capacitance=1µF part_number=0.33uF package="100 mil [THT, electrolytic]"]
  R223 = Resistor [tolerance=±5% resistance=220 package=THT]
  Q111 = NPN-Transistor [package="TO92 [THT]"]
  R235 = Resistor [tolerance=±5% resistance=220 package=THT]
  JP90 = Header 2 [package=screwterminal-3.5mm-2_lock]
  U23 = 74HC595 [package="DIP16 [THT]"]
  R256 = Resistor [tolerance=±5% resistance=220 package=THT]
  R238 = Resistor [tolerance=±5% resistance=220 package=THT]
  Q116 = NPN-Transistor [package="TO92 [THT]"]
  R252 = Resistor [tolerance=±5% resistance=220 package=THT]
  U25 = 74HC595 [package="DIP16 [THT]"]
  JP101 = Header 1 [package=pad-1.5x4.5]
  Q119 = NPN-Transistor [package="TO92 [THT]"]
  R243 = Resistor [tolerance=±5% resistance=220 package=THT]
  R237 = Resistor [tolerance=±5% resistance=220 package=THT]
  R247 = Resistor [tolerance=±5% resistance=220 package=THT]
  Q118 = NPN-Transistor [package="TO92 [THT]"]
  R258 = Resistor [tolerance=±5% resistance=220 package=THT]
  R226 = Resistor [tolerance=±5% resistance=220 package=THT]
  R225 = Resistor [tolerance=±5% resistance=220 package=THT]
  Q123 = NPN-Transistor [package="TO92 [THT]"]
  Q113 = NPN-Transistor [package="TO92 [THT]"]
  JP98 = Header 2 [package=springterminal-2.54mm-2]
  R234 = Resistor [tolerance=±5% resistance=220 package=THT]
  R251 = Resistor [tolerance=±5% resistance=220 package=THT]
  Q115 = NPN-Transistor [package="TO92 [THT]"]
  C37 = Ceramic Capacitor [capacitance=100nF package="100 mil [THT, multilayer]"]
  R244 = Resistor [tolerance=±5% resistance=220 package=THT]
  R257 = Resistor [tolerance=±5% resistance=220 package=THT]
  R230 = Resistor [tolerance=±5% resistance=220 package=THT]
  C35 = Ceramic Capacitor [capacitance=100nF package="100 mil [THT, multilayer]"]
  R240 = Resistor [tolerance=±5% resistance=220 package=THT]
  JP95 = Header 2 [package=springterminal-2.54mm-2]
  JP94 = Header 2 [package=springterminal-2.54mm-2]
  JP97 = Header 2 [package=springterminal-2.54mm-2]
  R260 = Resistor [tolerance=±5% resistance=220 package=THT]
  R248 = Resistor [tolerance=±5% resistance=220 package=THT]
  Q110 = NPN-Transistor [package="TO92 [THT]"]
  Q125 = NPN-Transistor [package="TO92 [THT]"]
  R253 = Resistor [tolerance=±5% resistance=220 package=THT]
  R236 = Resistor [tolerance=±5% resistance=220 package=THT]
  C36 = Ceramic Capacitor [capacitance=100nF package="100 mil [THT, multilayer]"]
  R224 = Resistor [tolerance=±5% resistance=220 package=THT]
  JP91 = Header 2 [package=springterminal-2.54mm-2]
  R241 = Resistor [tolerance=±5% resistance=220 package=THT]
  Q120 = NPN-Transistor [package="TO92 [THT]"]
  R228 = Resistor [tolerance=±5% resistance=220 package=THT]
  JP100 = Header 2 [package=springterminal-2.54mm-2]
  R231 = Resistor [tolerance=±5% resistance=220 package=THT]
  R246 = Resistor [tolerance=±5% resistance=220 package=THT]
  Q126 = NPN-Transistor [package="TO92 [THT]"]
  R239 = Resistor [tolerance=±5% resistance=220 package=THT]
  JP92 = Header 2 [package=springterminal-2.54mm-2]
  Q109 = NPN-Transistor [package="TO92 [THT]"]
  R222 = Resistor [tolerance=±5% resistance=220 package=THT]
  R255 = Resistor [tolerance=±5% resistance=220 package=THT]
  R259 = Resistor [tolerance=±5% resistance=220 package=THT]
  R232 = Resistor [tolerance=±5% resistance=220 package=THT]
  Q114 = NPN-Transistor [package="TO92 [THT]"]
  Q117 = NPN-Transistor [package="TO92 [THT]"]
  U24 = 74HC595 [package="DIP16 [THT]"]
  JP99 = Header 2 [package=springterminal-2.54mm-2]
  Q108 = NPN-Transistor [package="TO92 [THT]"]
  U26 = Voltage Regulator - 5V [package="DPak [SMD]"]
  R249 = Resistor [tolerance=±5% resistance=220 package=THT]
  Q107 = NPN-Transistor [package="TO92 [THT]"]
  JP93 = Header 2 [package=springterminal-2.54mm-2]
  R242 = Resistor [tolerance=±5% resistance=220 package=THT]
  R229 = Resistor [tolerance=±5% resistance=220 package=THT]
  R221 = Resistor [tolerance=±5% resistance=220 package=THT]
  JP96 = Header 2 [package=springterminal-2.54mm-2]
  R233 = Resistor [tolerance=±5% resistance=220 package=THT]
  Q124 = NPN-Transistor [package="TO92 [THT]"]

nets:
  GND: Componente1.GND, U6.INH, U6.VEE, U6.VSS, JP35.3, Q24.E, Q25.E, Q26.E, JP40.2, C12.1, JP41.1, C34.-, C33.-, JP90.1, U23.GND, U23.OE, U25.GND, U25.OE, JP101.1, C37.0, C35.0, C36.0, U24.GND, U24.OE, U26.GND
  START: Componente1.D2, JP40.1, R60.Pin_0
  CLK: Componente1.D4, JP36.5, U23.SH_CP, U25.SH_CP, U24.SH_CP
  DATA: Componente1.D5, JP36.4, U25.DS
  LATCH: Componente1.D6, U23.ST_CP, U25.ST_CP, U24.ST_CP
  N1: Componente1.D7, JP36.3
  N2: Componente1.D8, JP36.2
  N3: Componente1.D9, JP36.1
  MOTOR: Componente1.D10, R56.Pin_1
  LASER: Componente1.D12/MISO, R58.Pin_1
  5V: Componente1.VIN, U6.VDD, R46.Pin_1, R47.Pin_1, R48.Pin_1, R49.Pin_1, R50.Pin_1, R51.Pin_0, R52.Pin_0, R53.Pin_0, R54.Pin_0, R55.Pin_0, JP35.1, JP38.1, R60.Pin_1, C12.0, R245.Pin_0, R254.Pin_0, R250.Pin_0, C33.+, U23.MR, U23.VCC, R256.Pin_0, R252.Pin_0, U25.MR, U25.VCC, R243.Pin_0, R247.Pin_0, R258.Pin_0, R251.Pin_0, C37.1, R244.Pin_0, R257.Pin_0, C35.1, R260.Pin_0, R248.Pin_0, R253.Pin_0, C36.1, R241.Pin_0, R246.Pin_0, R255.Pin_0, R259.Pin_0, U24.MR, U24.VCC, U26.output_voltage, R249.Pin_0, R242.Pin_0
  LDR10: Componente1.A5, R51.Pin_1, JP30.10
  LDR9: Componente1.A4, R52.Pin_1, JP30.9
  ENTRADA: Componente1.A3, U6.IO
  SEL_C: Componente1.A2, U6.C
  SEL_B: Componente1.A1, U6.B
  SEL_A: Componente1.A0, U6.A
  BUZZER: Componente1.D11/MOSI, R57.Pin_1
  LDR1: U6.IO4, R46.Pin_0, JP30.1
  LDR2: U6.IO6, R47.Pin_0, JP30.2
  LDR3: U6.IO7, R48.Pin_0, JP30.3
  LDR4: U6.IO5, R49.Pin_0, JP30.4
  LDR8: U6.IO3, R53.Pin_1, JP30.8
  LDR7: U6.IO0, R54.Pin_1, JP30.7
  LDR6: U6.IO1, R55.Pin_1, JP30.6
  LDR5: U6.IO2, R50.Pin_0, JP30.5
  12V: JP35.2, JP37.1, D1.cathode, JP39.1
  N4: JP37.2, D1.anode, Q24.C
  N5: JP38.2, Q25.C
  N6: Q24.B, R56.Pin_0
  N7: Q25.B, R57.Pin_0
  N8: Q26.B, R58.Pin_0
  N9: Q26.C, R59.Pin_0
  N10: JP39.2, R59.Pin_1
  N11: Q121.E, JP97.1
  N12: Q121.B, R237.Pin_0
  N13: Q121.C, R255.Pin_1
  N14: R245.Pin_1, Q111.C
  N15: Q122.E, JP95.1
  N16: Q122.B, R235.Pin_0
  N17: Q122.C, R256.Pin_1
  N18: R254.Pin_1, Q119.C
  N19: R250.Pin_1, Q112.C
  N20: R227.Pin_0, Q111.B
  L3_B: R227.Pin_1, U25.Q6
  N21: Q112.E, JP95.2
  N22: Q112.B, R223.Pin_0
  N23: C34.+, JP90.2, U26.input_voltage
  L6_B: R223.Pin_1, U24.Q5
  N24: Q111.E, JP98.2
  L8_A: U23.Q1
  L8_B: U23.Q2, R222.Pin_1
  L9_A: U23.Q3
  L9_B: U23.Q4, R229.Pin_1
  L10_A: U23.Q5
  L10_B: U23.Q6
  N25: U23.DS, U24.Q7'
  N26: R238.Pin_0, Q124.B
  L3_A: R238.Pin_1, U25.Q5
  N27: Q116.E, JP94.2
  N28: Q116.B, R230.Pin_0
  N29: Q116.C, R242.Pin_1
  N30: R252.Pin_1, Q118.C
  L1_A: U25.Q1, R240.Pin_1
  L1_B: U25.Q2, R224.Pin_1
  L2_A: U25.Q3
  L2_B: U25.Q4, R226.Pin_1
  L4_A: U25.Q7, R237.Pin_1
  N31: U25.Q7', U24.DS
  N32: Q119.E, JP94.1
  N33: Q119.B, R232.Pin_0
  N34: R243.Pin_1, Q110.C
  N35: R247.Pin_1, Q114.C
  N36: Q118.E, JP91.1
  N37: Q118.B, R234.Pin_0
  N38: R258.Pin_1, Q124.C
  N39: R226.Pin_0, Q113.B
  N40: R225.Pin_0, Q114.B
  L4_B: R225.Pin_1, U24.Q1
  N41: Q123.E, JP96.1
  N42: Q123.B, R236.Pin_0
  N43: Q123.C, R257.Pin_1
  N44: Q113.E, JP99.2
  N45: Q113.C, R248.Pin_1
  N46: JP98.1, Q124.E
  N47: Q115.E, JP92.2
  N48: Q115.B, R229.Pin_0
  N49: Q115.C, R244.Pin_1
  L7_B: R230.Pin_1, U24.Q7
  N50: R240.Pin_0, Q126.B
  N51: JP97.2, Q114.E
  N52: R260.Pin_1, Q126.C
  N53: Q110.E, JP93.2
  N54: Q110.B, R222.Pin_0
  N55: Q125.E, JP99.1
  N56: Q125.B, R239.Pin_0
  N57: Q125.C, R259.Pin_1
  N58: R253.Pin_1, Q117.C
  L5_A: R236.Pin_1, U24.Q2
  N59: R224.Pin_0, Q109.B
  N60: JP91.2, Q107.E
  N61: R241.Pin_1, Q107.C
  N62: Q120.E, JP92.1
  N63: Q120.B, R233.Pin_0
  N64: R228.Pin_0, Q108.B
  L5_B: R228.Pin_1, U24.Q3
  N65: JP100.1, Q126.E
  N66: JP100.2, Q109.E
  N67: R231.Pin_0, Q117.B
  N68: R246.Pin_1, Q108.C
  N69: Q109.C, R249.Pin_1
  N70: Q117.E, JP93.1
  L6_A: U24.Q4
  L7_A: U24.Q6
  N71: Q108.E, JP96.2
  N72: Q107.B, R221.Pin_0

notes:
  LED1
  12V
  5V
  GND
  Conectar a todos os displays
  A
  B
  C
  D
  E
  A - pino 11 do 595
  B - pino 14 de um dos 595 do conjunto
  C, D, E - cada um para o pino 12 de cada conjunto
  MOTOR
  BUZZER
  LASER
  START
  CONECTOR DISPLAYS
  CONECTOR DOS LDRS
  COMUM
  LED10
  LED9
  LED8
  LED7
  LED6
  LED5
  LED4
  LED3
  LED2
  Base: 1,5 Kohm
  Vermelho: 51 ohm
  azul/verde: 27 ohm
  transistor: BC548
  REGULADOR 7805
  0.33uF
  0.1uF
