# Fritzing sketch placaPrincipal_v2 (saved by Fritzing 0.9.3b)
breadboards: 1

parts:
  Componente1 = Arduino Nano (Rev3.0) (ICSP)
  U6 = 74HC4051 [package=so16]
  R46 = Resistor [tolerance=±5% resistance=3.3k package=THT]
  R47 = Resistor [tolerance=±5% resistance=220 package=THT]
  R48 = Resistor [tolerance=±5% resistance=220 package=THT]
  R49 = Resistor [tolerance=±5% resistance=220 package=THT]
  R50 = Resistor [tolerance=±5% resistance=220 package=THT]
  R51 = Resistor [tolerance=±5% resistance=3.3k package=THT]
  R52 = Resistor [tolerance=±5% resistance=220 package=THT]
  R53 = Resistor [tolerance=±5% resistance=220 package=THT]
  R54 = Resistor [tolerance=±5% resistance=220 package=THT]
  R55 = Resistor [tolerance=±5% resistance=220 package=THT]
  JP30 = Header 10 [package=1x10-2mm-smd]
  JP35 = Header 3 [package=screwterminal-3.5mm-3_lock.007s]
  JP36 = Header 5 [package=1x05-1mm]
  JP37 = Header 2 [package=springterminal-2.54mm-2]
  D1 = Rectifier Diode [part_number=1N4001 package="Melf DO-213 AB [SMD]"]
  JP38 = Header 2 [package=springterminal-2.54mm-2]
  Q24 = NPN-Transistor [part_number=TIP122 package="TO92 [THT]"]
  R56 = Resistor [tolerance=±5% resistance=2.2k package=THT]
  Q25 = NPN-Transistor [part_number=TIP122 package="TO92 [THT]"]
  R57 = Resistor [tolerance=±2% resistance=1.5k package=THT]
  Q26 = NPN-Transistor [part_number=BC548 package="TO92 [THT]"]
  R58 = Resistor [tolerance=±5% resistance=1.5k package=THT]
  JP39 = Header 2 [package=springterminal-2.54mm-2]
  R59 = Resistor [tolerance=±5% resistance=470 package=THT]
  JP40 = Header 2 [package=springterminal-2.54mm-2]
  R60 = Resistor [tolerance=±5% resistance=10k package=THT]
  C12 = Ceramic Capacitor [capacitance=100nF package="100 mil [THT, multilayer]"]
  JP41 = Header 1 [package=pad-1.5x4.5]
  C34 = Electrolytic Capacitor [capacitance=1µF part_number=0.33uF package="100 mil [THT, electrolytic]"]
  C33 = Electrolytic Capacitor [capacitance=1µF part_number=0.33uF package="100 mil [THT, electrolytic]"]
  JP90 = Header 2 [package=screwterminal-3.5mm-2_lock]
  U23 = 74HC595 [package="DIP16 [THT]"]
  U25 = 74HC595 [package="DIP16 [THT]"]
  C37 = Ceramic Capacitor [capacitance=100nF package="100 mil [THT, multilayer]"]
  C35 = Ceramic Capacitor [capacitance=100nF package="100 mil [THT, multilayer]"]
  C36 = Ceramic Capacitor [capacitance=100nF package="100 mil [THT, multilayer]"]
  U24 = 74HC595 [package="DIP16 [THT]"]
  U26 = Voltage Regulator - 5V [package="DPak [SMD]"]
  IC1 = ULN2003A [package="SO16 [SMD]"]
  IC2 = ULN2003A [package="SO16 [SMD]"]
  IC3 = ULN2003A [package="SO16 [SMD]"]
  JP102 = Header 2 [package=springterminal-2.54mm-2]
  JP103 = Header 2 [package=springterminal-2.54mm-2]
  JP104 = Header 2 [package=springterminal-2.54mm-2]
  JP105 = Header 2 [package=springterminal-2.54mm-2]
  JP106 = Header 2 [package=springterminal-2.54mm-2]
  JP107 = Header 2 [package=springterminal-2.54mm-2]
  JP108 = Header 2 [package=springterminal-2.54mm-2]
  JP109 = Header 2 [package=springterminal-2.54mm-2]
  JP110 = Header 2 [package=springterminal-2.54mm-2]
  JP111 = Header 2 [package=springterminal-2.54mm-2]
  JP112 = Header 1 [package=pad-1.5x4.5]
  R61 = Resistor [tolerance=±5% resistance=220 package=THT]
  R62 = Resistor [tolerance=±5% resistance=220 package=THT]
  R63 = Resistor [tolerance=±5% resistance=220 package=THT]
  R64 = Resistor [tolerance=±5% resistance=220 package=THT]
  R65 = Resistor [tolerance=±5% resistance=220 package=THT]
  R66 = Resistor [tolerance=±5% resistance=220 package=THT]
  R69 = Resistor [tolerance=±5% resistance=220 package=THT]
  R70 = Resistor [tolerance=±5% resistance=220 package=THT]
  R71 = Resistor [tolerance=±5% resistance=220 package=THT]
  R72 = Resistor [tolerance=±5% resistance=220 package=THT]
  R75 = Resistor [tolerance=±5% resistance=220 package=THT]
  R76 = Resistor [tolerance=±5% resistance=220 package=THT]
  R77 = Resistor [tolerance=±5% resistance=220 package=THT]
  R78 = Resistor [tolerance=±5% resistance=220 package=THT]
  R79 = Resistor [tolerance=±5% resistance=220 package=THT]
  R80 = Resistor [tolerance=±5% resistance=220 package=THT]
  R81 = Resistor [tolerance=±5% resistance=220 package=THT]
  R82 = Resistor [tolerance=±5% resistance=220 package=THT]
  R83 = Resistor [tolerance=±5% resistance=220 package=THT]
  R84 = Resistor [tolerance=±5% resistance=220 package=THT]

nets:
  GND: Componente1.GND, U6.INH, U6.VEE, U6.VSS, JP35.3, Q24.E, Q25.E, Q26.E, JP40.2, C12.1, JP41.1, C34.-, C33.-, JP90.1, U23.GND, U23.OE, U25.GND, U25.OE, C37.0, C35.0, C36.0, U24.GND, U24.OE, U26.GND, IC1.0V, IC2.0V, IC3.0V
  START: Componente1.D2, JP40.1, R60.Pin_0
  CLK: Componente1.D4, JP36.5, U23.SH_CP, U25.SH_CP, U24.SH_CP
  DATA: Componente1.D5, JP36.4, U25.DS
  LATCH: Componente1.D6, U23.ST_CP, U25.ST_CP, U24.ST_CP
  N1: Componente1.D7, JP36.3
  N2: Componente1.D8, JP36.2
  N3: Componente1.D9, JP36.1
  MOTOR: Componente1.D10, R56.Pin_1
  LASER: Componente1.D12/MISO, R58.Pin_1
  5V: Componente1.VIN, U6.VDD, R46.Pin_1, R47.Pin_1, R48.Pin_1, R49.Pin_1, R50.Pin_1, R51.Pin_0, R52.Pin_0, R53.Pin_0, R54.Pin_0, R55.Pin_0, JP35.1, JP38.1, R60.Pin_1, C12.0, C33.+, U23.MR, U23.VCC, U25.MR, U25.VCC, C37.1, C35.1, C36.1, U24.MR, U24.VCC, U26.output_voltage, IC1.COM_-_Common, IC2.COM_-_Common, IC3.COM_-_Common, JP112.1
  LDR10: Componente1.A5, R51.Pin_1, JP30.10
  LDR9: Componente1.A4, R52.Pin_1, JP30.9
  ENTRADA: Componente1.A3, U6.IO
  SEL_C: Componente1.A2, U6.C
  SEL_B: Componente1.A1, U6.B
  SEL_A: Componente1.A0, U6.A
  BUZZER: Componente1.D11/MOSI, R57.Pin_1
  LDR1: U6.IO4, R46.Pin_0, JP30.1
  LDR2: U6.IO6, R47.Pin_0, JP30.2
  LDR3: U6.IO7, R48.Pin_0, JP30.3
  LDR4: U6.IO5, R49.Pin_0, JP30.4
  LDR8: U6.IO3, R53.Pin_1, JP30.8
  LDR7: U6.IO0, R54.Pin_1, JP30.7
  LDR6: U6.IO1, R55.Pin_1, JP30.6
  LDR5: U6.IO2, R50.Pin_0, JP30.5
  12V: JP35.2, JP37.1, D1.cathode, JP39.1
  N4: JP37.2, D1.anode, Q24.C
  N5: JP38.2, Q25.C
  N6: Q24.B, R56.Pin_0
  N7: Q25.B, R57.Pin_0
  N8: Q26.B, R58.Pin_0
  N9: Q26.C, R59.Pin_0
  N10: JP39.2, R59.Pin_1
  N11: C34.+, JP90.2, U26.input_voltage
  N12: U23.Q1, IC3.In_7
  N13: U23.Q2, IC3.In_6
  N14: U23.Q3, IC3.In_5
  N15: U23.Q4, IC3.In_4
  N16: U23.Q5, IC3.In_3
  N17: U23.Q6, IC3.In_2
  N18: U23.DS, U24.Q7'
  N19: U25.Q1, IC1.In_7
  N20: U25.Q2, IC1.In_6
  N21: U25.Q3, IC1.In_5
  N22: U25.Q4, IC1.In_4
  N23: U25.Q5, IC1.In_3
  N24: U25.Q6, IC1.In_2
  N25: U25.Q7, IC1.In_1
  N26: U25.Q7', U24.DS
  N27: U24.Q1, IC2.In_7
  N28: U24.Q2, IC2.In_6
  N29: U24.Q3, IC2.In_5
  N30: U24.Q4, IC2.In_4
  N31: U24.Q5, IC2.In_3
  N32: U24.Q6, IC2.In_2
  N33: U24.Q7, IC2.In_1
  N34: IC1.Out_7, R71.Pin_1
  N35: IC1.Out_6, R72.Pin_1
  N36: IC1.Out_5, R75.Pin_1
  N37: IC1.Out_4, R76.Pin_1
  N38: IC1.Out_3, R77.Pin_1
  N39: IC1.Out_2, R78.Pin_1
  N40: IC1.Out_1, R79.Pin_1
  N41: IC2.Out_7, R80.Pin_1
  N42: IC2.Out_6, R81.Pin_1
  N43: IC2.Out_5, R82.Pin_1
  N44: IC2.Out_4, R83.Pin_1
  N45: IC2.Out_3, R84.Pin_1
  N46: IC2.Out_2, R69.Pin_1
  N47: IC2.Out_1, R70.Pin_1
  N48: IC3.Out_7, R66.Pin_1
  N49: IC3.Out_6, R65.Pin_1
  N50: IC3.Out_5, R64.Pin_1
  N51: IC3.Out_4, R63.Pin_1
  N52: IC3.Out_3, R62.Pin_1
  N53: IC3.Out_2, R61.Pin_1
  N54: JP102.1, R62.Pin_0
  N55: JP102.2, R61.Pin_0
  N56: JP103.1, R64.Pin_0
  N57: JP103.2, R63.Pin_0
  N58: JP104.1, R66.Pin_0
  N59: JP104.2, R65.Pin_0
  N60: JP105.1, R69.Pin_0
  N61: JP105.2, R70.Pin_0
  N62: JP106.1, R83.Pin_0
  N63: JP106.2, R84.Pin_0
  N64: JP107.1, R81.Pin_0
  N65: JP107.2, R82.Pin_0
  N66: JP108.1, R79.Pin_0
  N67: JP108.2, R80.Pin_0
  N68: JP109.1, R77.Pin_0
  N69: JP109.2, R78.Pin_0
  N70: JP110.1, R75.Pin_0
  N71: JP110.2, R76.Pin_0
  N72: JP111.1, R71.Pin_0
  N73: JP111.2, R72.Pin_0

notes:
  LED1
  12V
  5V
  GND
  Conectar a todos os displays
  A
  B
  C
  D
  E
  A - pino 11 do 595
  B - pino 14 de um dos 595 do conjunto
  C, D, E - cada um para o pino 12 de cada conjunto
  MOTOR
  BUZZER
  LASER
  START
  CONECTOR DISPLAYS
  CONECTOR DOS LDRS
  COMUM
  LED10
  LED9
  LED8
  LED7
  LED6
  LED5
  LED4
  LED3
  LED2
  Base: 1,5 Kohm
  Vermelho: 51 ohm
  azul/verde: 27 ohm
  transistor: BC548
  REGULADOR 7805
  0.33uF
  0.1uF
  Vermelho: 100 ohm
  azul/verde: 68 ohm
  COR 1
  COR 2
