# Fritzing sketch display_novo (saved by Fritzing 0.9.3b)
breadboards: 1

parts:
  U1 = 7-SEGMENT-DISPLAY [package=7-segment-display]
  U2 = 74HC595 [package="DIP16 [THT]"]
  IC1 = ULN2003A [package="DIP16 [THT]"]
  R10 = Resistor [tolerance=±5% resistance=1k package=THT]
  R2 = Resistor [tolerance=±5% resistance=1k package=THT]
  R4 = Resistor [tolerance=±5% resistance=1k package=THT]
  R5 = Resistor [tolerance=±5% resistance=1k package=THT]
  R7 = Resistor [tolerance=±5% resistance=1k package=THT]
  R8 = Resistor [tolerance=±5% resistance=1k package=THT]
  R9 = Resistor [tolerance=±5% resistance=1k package=THT]
  C4 = Ceramic Capacitor [capacitance=100nF package="100 mil [THT, multilayer]"]
  JP1 = Header 3 [package=screwterminal-3.5mm-3_lock.007s]
  JP2 = Header 3 [package=screwterminal-3.5mm-3_lock.007s]
  U3 = 7-SEGMENT-DISPLAY [package=7-segment-display]
  U4 = 74HC595 [package="DIP16 [THT]"]
  IC2 = ULN2003A [package="DIP16 [THT]"]
  R11 = Resistor [tolerance=±5% resistance=1k package=THT]
  R12 = Resistor [tolerance=±5% resistance=1k package=THT]
  R13 = Resistor [tolerance=±5% resistance=1k package=THT]
  R14 = Resistor [tolerance=±5% resistance=1k package=THT]
  R15 = Resistor [tolerance=±5% resistance=1k package=THT]
  R16 = Resistor [tolerance=±5% resistance=1k package=THT]
  R17 = Resistor [tolerance=±5% resistance=1k package=THT]

nets:
  N1: U1.E, R8.Pin_1
  N2: U1.D, R4.Pin_1
  N3: U1.G1, U1.G2, IC1.COM_-_Common, JP2.2, U3.G1, U3.G2, IC2.COM_-_Common
  N4: U1.C, R5.Pin_1
  N5: U1.B, R2.Pin_1
  N6: U1.A, R10.Pin_1
  N7: U1.F, R7.Pin_1
  N8: U1.G, R9.Pin_1
  N9: U2.Q1, IC1.In_1
  N10: U2.Q2, IC1.In_2
  N11: U2.Q3, IC1.In_3
  N12: U2.Q4, IC1.In_4
  N13: U2.Q5, IC1.In_5
  N14: U2.Q6, IC1.In_6
  N15: U2.Q7, IC1.In_7
  GND: U2.GND, U2.OE, IC1.0V, C4.0, JP2.3, U4.GND, U4.OE, IC2.0V
  N16: U2.Q7', U4.DS
  VCC: U2.MR, U2.VCC, C4.1, JP2.1, U4.MR, U4.VCC
  N17: U2.SH_CP, JP1.3, U4.SH_CP
  N18: U2.ST_CP, JP1.2, U4.ST_CP
  N19: U2.DS, JP1.1
  N20: IC1.Out_7, R9.Pin_0
  N21: IC1.Out_6, R7.Pin_0
  N22: IC1.Out_5, R8.Pin_0
  N23: IC1.Out_4, R4.Pin_0
  N24: IC1.Out_3, R5.Pin_0
  N25: IC1.Out_2, R2.Pin_0
  N26: IC1.Out_1, R10.Pin_0
  N27: U3.E, R12.Pin_1
  N28: U3.D, R15.Pin_1
  N29: U3.C, R14.Pin_1
  N30: U3.B, R16.Pin_1
  N31: U3.A, R17.Pin_1
  N32: U3.F, R13.Pin_1
  N33: U3.G, R11.Pin_1
  N34: U4.Q1, IC2.In_1
  N35: U4.Q2, IC2.In_2
  N36: U4.Q3, IC2.In_3
  N37: U4.Q4, IC2.In_4
  N38: U4.Q5, IC2.In_5
  N39: U4.Q6, IC2.In_6
  N40: U4.Q7, IC2.In_7
  N41: IC2.Out_7, R11.Pin_0
  N42: IC2.Out_6, R13.Pin_0
  N43: IC2.Out_5, R12.Pin_0
  N44: IC2.Out_4, R15.Pin_0
  N45: IC2.Out_3, R14.Pin_0
  N46: IC2.Out_2, R16.Pin_0
  N47: IC2.Out_1, R17.Pin_0

notes:
  12V
  GND
  5V
  C, D
  A
  B
